# Fritzing sketch ESP32 CAM Programming Circuit (saved by Fritzing 0.9.3b)

parts:
  Part1 = Arduino Ethernet Shield (Rev3)
  WeMos_D1_Mini1 = WeMos D1 Mini

nets:
  N1: Part1.RX/D0, WeMos_D1_Mini1.TX
  N2: Part1.TX/D1, WeMos_D1_Mini1.RX
  N3: Part1.RESET, Part1.GND, WeMos_D1_Mini1.G
  3V3: Part1.3V3, WeMos_D1_Mini1.3V3
