# Fritzing sketch Face Mask Detector Circuit Diagram (saved by Fritzing 0.9.3b)

parts:
  LED2 = LED - 3mm [color="Green (555nm)" package="3 mm [THT]"]
  WeMos_D1_Mini1 = WeMos D1 Mini
  Part1 = Arduino Ethernet Shield (Rev3)

nets:
  N1: LED2.cathode, WeMos_D1_Mini1.RX
  N2: LED2.anode, WeMos_D1_Mini1.G
  3V3: WeMos_D1_Mini1.3V3, Part1.3V3
  N3: Part1.RESET, Part1.GND
